// Digital circuit Problema 1 - Portas NAND.dig as structural Verilog
module Problema_1___Portas_NAND (
  input  A,
  input  B,
  input  C,
  input  D
);

  wire nand_1_out, nand_2_out, nand_3_out, nand_4_out, nand_5_out, nand_6_out, nand_7_out;

  nand nand_1 (nand_1_out, A, B);
  nand nand_2 (nand_2_out, B, C, D);
  nand nand_3 (nand_3_out, nand_1_out, nand_1_out);
  nand nand_4 (nand_4_out, nand_2_out, nand_2_out);
  nand nand_5 (nand_5_out, nand_3_out, nand_3_out);
  nand nand_6 (nand_6_out, nand_4_out, nand_4_out);
  nand nand_7 (nand_7_out, nand_5_out, nand_6_out);
  LED S (.in(nand_7_out));

  // Notes on the sheet:
  //   A: Ja passa das 17h
  //   B: Todas as máquinas estão desligadas
  //   C: É sexta feira
  //   D: Produção do dia foi atendida
  //   Integrante: Yuri Cristian Pedrosa de Oliveira
endmodule
