// Digital circuit Problema 1 - Portas NOR.dig as structural Verilog
module Problema_1___Portas_NOR (
  input  A,
  input  B,
  input  C,
  input  D
);

  wire nor_1_out, nor_2_out, nor_3_out, nor_4_out, nor_5_out, nor_6_out, nor_7_out, nor_8_out, nor_9_out;

  nor nor_1 (nor_1_out, A, A);
  nor nor_2 (nor_2_out, B, B);
  nor nor_3 (nor_3_out, B, B);
  nor nor_4 (nor_4_out, C, C);
  nor nor_5 (nor_5_out, D, D);
  nor nor_6 (nor_6_out, nor_1_out, nor_2_out);
  nor nor_7 (nor_7_out, nor_3_out, nor_4_out, nor_5_out);
  nor nor_8 (nor_8_out, nor_6_out, nor_7_out);
  nor nor_9 (nor_9_out, nor_8_out, nor_8_out);
  LED S (.in(nor_9_out));

  // Notes on the sheet:
  //   A: Ja passa das 17h
  //   B: Todas as máquinas estão desligadas
  //   C: É sexta feira
  //   D: Produção do dia foi atendida
  //   Integrante: Yuri Cristian Pedrosa de Oliveira
endmodule
