// Digital circuit Problema 1.dig as structural Verilog
module Problema_1 (
  input  A,
  input  B,
  input  C,
  input  D
);

  wire and_1_out, and_2_out, or_1_out;

  and and_1 (and_1_out, A, B);
  and and_2 (and_2_out, B, C, D);
  or or_1 (or_1_out, and_1_out, and_2_out);
  LED S (.in(or_1_out));

  // Notes on the sheet:
  //   A: Ja passa das 17h
  //   B: Todas as máquinas estão desligadas
  //   C: É sexta feira
  //   D: Produção do dia foi atendida
  //   Integrante: Yuri Cristian Pedrosa de Oliveira
endmodule
