// Digital circuit Problema 2 - E2 - Portas NOR.dig as structural Verilog
module Problema_2___E2___Portas_NOR (
  input  x1,
  input  x2,
  input  x3
);

  wire nor_1_out, nor_2_out, nor_3_out, nor_4_out, nor_5_out, nor_6_out, nor_7_out, nor_8_out, nor_9_out,
       nor_10_out, nor_11_out, nor_12_out, nor_13_out, nor_14_out, nor_15_out, nor_16_out;

  nor nor_1 (nor_1_out, x1, x1);
  nor nor_2 (nor_2_out, x2, x2);
  nor nor_3 (nor_3_out, x3, x3);
  nor nor_4 (nor_4_out, x1, x1);
  nor nor_5 (nor_5_out, nor_2_out, nor_2_out);
  nor nor_6 (nor_6_out, x3, x3);
  nor nor_7 (nor_7_out, x1, x1);
  nor nor_8 (nor_8_out, nor_3_out, nor_3_out);
  nor nor_9 (nor_9_out, nor_1_out, nor_1_out);
  nor nor_10 (nor_10_out, x2, x2);
  nor nor_11 (nor_11_out, nor_4_out, nor_5_out);
  nor nor_12 (nor_12_out, nor_5_out, nor_6_out);
  nor nor_13 (nor_13_out, nor_6_out, nor_7_out);
  nor nor_14 (nor_14_out, nor_8_out, nor_9_out, nor_10_out);
  nor nor_15 (nor_15_out, nor_11_out, nor_12_out, nor_13_out, nor_14_out);
  nor nor_16 (nor_16_out, nor_15_out, nor_15_out);
  LED E2 (.in(nor_16_out));

  // Notes on the sheet:
  //   Integrante: Yuri Cristian Pedrosa de Oliveira
endmodule
