// Digital circuit Problema 2 - E3 - Portas NOR.dig as structural Verilog
module Problema_2___E3___Portas_NOR (
  input  x1,
  input  x2,
  input  x3
);

  wire nor_1_out, nor_2_out, nor_3_out, nor_4_out, nor_5_out, nor_6_out, nor_7_out, nor_8_out, nor_9_out,
       nor_10_out, nor_11_out;

  nor nor_1 (nor_1_out, x1, x1);
  nor nor_2 (nor_2_out, x2, x2);
  nor nor_3 (nor_3_out, x3, x3);
  nor nor_4 (nor_4_out, x1, x1);
  nor nor_5 (nor_5_out, nor_3_out, nor_3_out);
  nor nor_6 (nor_6_out, nor_1_out, nor_1_out);
  nor nor_7 (nor_7_out, x3, x3);
  nor nor_8 (nor_8_out, nor_4_out, nor_5_out);
  nor nor_9 (nor_9_out, nor_6_out, nor_7_out);
  nor nor_10 (nor_10_out, nor_8_out, nor_9_out);
  nor nor_11 (nor_11_out, nor_10_out, nor_10_out);
  LED E3 (.in(nor_11_out));

  // Notes on the sheet:
  //   Integrante: Yuri Cristian Pedrosa de Oliveira
endmodule
