// Digital circuit Problema 2.dig as structural Verilog
module Problema_2 (
  input  x1,
  input  x2,
  input  x3
);

  wire and_1_out, and_2_out, and_3_out, not_1_out, not_2_out, not_3_out, or_1_out;

  not not_1 (not_1_out, x1);
  not not_2 (not_2_out, x2);
  not not_3 (not_3_out, x3);
  and and_1 (and_1_out, not_2_out, x3);
  and and_2 (and_2_out, x2, not_3_out);
  and and_3 (and_3_out, not_1_out, x2);
  or or_1 (or_1_out, and_1_out, and_2_out, and_3_out);
  LED E1 (.in(or_1_out));

  // Notes on the sheet:
  //   Integrante: Yuri Cristian Pedrosa de Oliveira
endmodule
