// Digital circuit Problema 2 - E1 - Portas NAND.dig as structural Verilog
module Problema_2___E1___Portas_NAND (
  input  x1,
  input  x2,
  input  x3
);

  wire nand_1_out, nand_2_out, nand_3_out, nand_4_out, nand_5_out, nand_6_out, nand_7_out, nand_8_out,
       nand_9_out, nand_10_out, nand_11_out, nand_12_out, nand_13_out;

  nand nand_1 (nand_1_out, x1, x1);
  nand nand_2 (nand_2_out, x2, x2);
  nand nand_3 (nand_3_out, x3, x3);
  nand nand_4 (nand_4_out, nand_2_out, x3);
  nand nand_5 (nand_5_out, x2, nand_3_out);
  nand nand_6 (nand_6_out, nand_1_out, x2);
  nand nand_7 (nand_7_out, nand_4_out, nand_4_out);
  nand nand_8 (nand_8_out, nand_5_out, nand_5_out);
  nand nand_9 (nand_9_out, nand_6_out, nand_6_out);
  nand nand_10 (nand_10_out, nand_7_out, nand_7_out);
  nand nand_11 (nand_11_out, nand_8_out, nand_8_out);
  nand nand_12 (nand_12_out, nand_9_out, nand_9_out);
  nand nand_13 (nand_13_out, nand_10_out, nand_11_out, nand_12_out);
  LED E1 (.in(nand_13_out));

  // Notes on the sheet:
  //   Integrante: Yuri Cristian Pedrosa de Oliveira
endmodule
